// Logisim project calculator.circ as structural Verilog
module halfAdder (
  input  i1,
  input  i2,
  output o,
  output c
);

  wire and_2_out, and_3_out, not_1_out;

  and and_1 (c, i1, i2);
  not not_1 (not_1_out, c);
  and and_2 (and_2_out, i1, not_1_out);
  and and_3 (and_3_out, not_1_out, i2);
  or or_1 (o, and_2_out, and_3_out);
endmodule

module fullAdder (
  input  cIn,
  input  i0,
  input  i1,
  output o,
  output cOut
);

  wire halfadder_1_c, halfadder_1_o, halfadder_2_c;

  halfAdder halfadder_1 (.i1(i0), .i2(i1), .o(halfadder_1_o), .c(halfadder_1_c));
  or or_1 (cOut, halfadder_1_c, halfadder_2_c);
  halfAdder halfadder_2 (.i1(cIn), .i2(halfadder_1_o), .o(o), .c(halfadder_2_c));
endmodule

module IVbitAdder (
  input  cIn,
  input  [3:0] i0,
  input  [3:0] i1,
  output [3:0] o,
  output cOut
);

  wire fulladder_1_cout, fulladder_2_cout, fulladder_3_cout;

  fullAdder fulladder_1 (.i0(cIn), .i1(i0[0]), .cIn(i1[0]), .o(o[0]), .cOut(fulladder_1_cout));
  fullAdder fulladder_2 (.i0(fulladder_1_cout), .i1(i0[1]), .cIn(i1[1]), .o(o[1]), .cOut(fulladder_2_cout));
  fullAdder fulladder_3 (.i0(fulladder_2_cout), .i1(i0[2]), .cIn(i1[2]), .o(o[2]), .cOut(fulladder_3_cout));
  fullAdder fulladder_4 (.i0(fulladder_3_cout), .i1(i0[3]), .cIn(i1[3]), .o(o[3]), .cOut(cOut));
endmodule

module VIIIbitAdder (
  input  cIn,
  input  [7:0] i0,
  input  [7:0] i1,
  output [7:0] o,
  output cOut
);

  wire ivbitadder_1_cout;

  IVbitAdder ivbitadder_1 (.i0(i0[3:0]), .i1(i1[3:0]), .o(o[3:0]), .cOut(ivbitadder_1_cout), .cIn(cIn));
  IVbitAdder ivbitadder_2 (.i0(i0[7:4]), .i1(i1[7:4]), .o(o[7:4]), .cOut(cOut), .cIn(ivbitadder_1_cout));
endmodule

module XVIbitAdder (
  input  cIn,
  input  [15:0] i0,
  input  [15:0] i1,
  output [15:0] o,
  output cOut
);

  wire viiibitadder_1_cout;

  VIIIbitAdder viiibitadder_1 (.cIn(cIn), .i0(i0[7:0]), .i1(i1[7:0]), .o(o[7:0]), .cOut(viiibitadder_1_cout));
  VIIIbitAdder viiibitadder_2 (.cIn(viiibitadder_1_cout), .i0(i0[15:8]), .i1(i1[15:8]), .o(o[15:8]), .cOut(cOut));
endmodule

module XVIbitInverter (
  input  [15:0] i,
  output [15:0] o,
  output cOut
);

  wire [15:0] not_1_out;

  not not_1 (not_1_out[0], i[0]);
  not not_2 (not_1_out[1], i[1]);
  not not_3 (not_1_out[2], i[2]);
  not not_4 (not_1_out[3], i[3]);
  not not_5 (not_1_out[4], i[4]);
  not not_6 (not_1_out[5], i[5]);
  not not_7 (not_1_out[6], i[6]);
  not not_8 (not_1_out[7], i[7]);
  not not_9 (not_1_out[8], i[8]);
  not not_10 (not_1_out[9], i[9]);
  not not_11 (not_1_out[10], i[10]);
  not not_12 (not_1_out[11], i[11]);
  not not_13 (not_1_out[12], i[12]);
  not not_14 (not_1_out[13], i[13]);
  not not_15 (not_1_out[14], i[14]);
  not not_16 (not_1_out[15], i[15]);
  XVIbitAdder xvibitadder_1 (.cIn(1'b0), .i0(not_1_out), .i1(16'h1), .o(o), .cOut(cOut));
endmodule

module XVIbitSoustractor (
  input  cIn,
  input  [15:0] i0,
  input  [15:0] i1,
  output [15:0] o,
  output cOut
);

  wire viiibitsoustractor_1_cout;

  VIIIbitSoustractor viiibitsoustractor_1 (
    .cIn(cIn), .i0(i0[7:0]), .i1(i1[7:0]), .o(o[7:0]), .cOut(viiibitsoustractor_1_cout));
  VIIIbitSoustractor viiibitsoustractor_2 (
    .cIn(viiibitsoustractor_1_cout), .i0(i0[15:8]), .i1(i1[15:8]), .o(o[15:8]), .cOut(cOut));
endmodule

module fullSoustractor (
  input  i0,
  input  i1,
  input  cIn,
  output o,
  output cOut
);

  wire halfsoustractor_1_c, halfsoustractor_1_o, halfsoustractor_2_c;

  halfSoustractor halfsoustractor_1 (.i1(i0), .i2(i1), .o(halfsoustractor_1_o), .c(halfsoustractor_1_c));
  or or_1 (cOut, halfsoustractor_1_c, halfsoustractor_2_c);
  halfSoustractor halfsoustractor_2 (.i1(halfsoustractor_1_o), .i2(cIn), .o(o), .c(halfsoustractor_2_c));
endmodule

module halfSoustractor (
  input  i1,
  input  i2,
  output o,
  output c
);

  wire and_1_out, and_2_out, not_1_out;

  and and_1 (and_1_out, i1, i2);
  not not_1 (not_1_out, and_1_out);
  and and_2 (and_2_out, i1, not_1_out);
  or or_1 (o, and_2_out, c);
  and and_3 (c, not_1_out, i2);
endmodule

module IVbitSoustractor (
  input  cIn,
  input  [3:0] i0,
  input  [3:0] i1,
  output [3:0] o,
  output cOut
);

  wire fullsoustractor_1_cout, fullsoustractor_2_cout, fullsoustractor_3_cout;

  fullSoustractor fullsoustractor_1 (.i0(i0[0]), .i1(i1[0]), .cIn(cIn), .o(o[0]), .cOut(fullsoustractor_1_cout));
  fullSoustractor fullsoustractor_2 (
    .i0(i0[1]), .i1(i1[1]), .cIn(fullsoustractor_1_cout), .o(o[1]), .cOut(fullsoustractor_2_cout));
  fullSoustractor fullsoustractor_3 (
    .i0(i0[2]), .i1(i1[2]), .cIn(fullsoustractor_2_cout), .o(o[2]), .cOut(fullsoustractor_3_cout));
  fullSoustractor fullsoustractor_4 (.i0(i0[3]), .i1(i1[3]), .cIn(fullsoustractor_3_cout), .o(o[3]), .cOut(cOut));
endmodule

module VIIIbitSoustractor (
  input  cIn,
  input  [7:0] i0,
  input  [7:0] i1,
  output [7:0] o,
  output cOut
);

  wire ivbitsoustractor_1_cout;

  IVbitSoustractor ivbitsoustractor_1 (
    .cIn(cIn), .i0(i0[3:0]), .i1(i1[3:0]), .o(o[3:0]), .cOut(ivbitsoustractor_1_cout));
  IVbitSoustractor ivbitsoustractor_2 (
    .cIn(ivbitsoustractor_1_cout), .i0(i0[7:4]), .i1(i1[7:4]), .o(o[7:4]), .cOut(cOut));
endmodule

module XVIbitMutliplicator (
  input  [15:0] i0,
  input  [15:0] i1,
  output [15:0] o,
  output c
);

  wire [15:0] bitselector_1_out, bitselector_2_out, bitselector_3_out, bitselector_4_out, bitselector_5_out,
       bitselector_6_out, bitselector_7_out, bitselector_8_out, bitselector_9_out, bitselector_10_out,
       bitselector_11_out, bitselector_12_out, bitselector_13_out, bitselector_14_out, bitselector_15_out,
       bitselector_16_out, not_1_out, xvibitadder_1_o, xvibitadder_2_o, xvibitadder_3_o, xvibitadder_4_o,
       xvibitadder_5_o, xvibitadder_6_o, xvibitadder_7_o, xvibitadder_8_o, xvibitadder_9_o, xvibitadder_10_o,
       xvibitadder_11_o, xvibitadder_12_o, xvibitadder_13_o, xvibitadder_14_o;

  BitSelector #(.width(16), .group(16)) bitselector_1 (.in(i0), .out(bitselector_1_out), .sel(not_1_out[0]));
  BitSelector #(.width(16), .group(16)) bitselector_2 (.in(i0), .out(bitselector_2_out), .sel(not_1_out[1]));
  assign not_1_out = ~i1;  // NOT_Gate not_1, 16 bits wide
  BitSelector #(.width(16), .group(16)) bitselector_3 (.in(i0), .out(bitselector_3_out), .sel(not_1_out[2]));
  BitSelector #(.width(16), .group(16)) bitselector_4 (.in(i0), .out(bitselector_4_out), .sel(not_1_out[3]));
  XVIbitAdder xvibitadder_1 (
    .i0(bitselector_1_out), .i1({bitselector_2_out[14:0], 1'b0}), .o(xvibitadder_1_o));  // open: cIn, cOut
  BitSelector #(.width(16), .group(16)) bitselector_5 (.in(i0), .out(bitselector_5_out), .sel(not_1_out[4]));
  BitSelector #(.width(16), .group(16)) bitselector_6 (.in(i0), .out(bitselector_6_out), .sel(not_1_out[5]));
  BitSelector #(.width(16), .group(16)) bitselector_7 (.in(i0), .out(bitselector_7_out), .sel(not_1_out[6]));
  XVIbitAdder xvibitadder_2 (
    .i0(xvibitadder_1_o), .i1({bitselector_3_out[13:0], 2'b00}), .o(xvibitadder_2_o));  // open: cIn, cOut
  XVIbitAdder xvibitadder_3 (
    .i0(xvibitadder_2_o), .i1({bitselector_4_out[12:0], 3'b000}), .o(xvibitadder_3_o));  // open: cIn, cOut
  BitSelector #(.width(16), .group(16)) bitselector_8 (.in(i0), .out(bitselector_8_out), .sel(not_1_out[7]));
  BitSelector #(.width(16), .group(16)) bitselector_9 (.in(i0), .out(bitselector_9_out), .sel(not_1_out[8]));
  BitSelector #(.width(16), .group(16)) bitselector_10 (.in(i0), .out(bitselector_10_out), .sel(not_1_out[9]));
  XVIbitAdder xvibitadder_4 (
    .i0(xvibitadder_3_o), .i1({bitselector_5_out[11:0], 4'b0000}), .o(xvibitadder_4_o));  // open: cIn, cOut
  BitSelector #(.width(16), .group(16)) bitselector_11 (.in(i0), .out(bitselector_11_out), .sel(not_1_out[10]));
  BitSelector #(.width(16), .group(16)) bitselector_12 (.in(i0), .out(bitselector_12_out), .sel(not_1_out[11]));
  XVIbitAdder xvibitadder_5 (
    .i0(xvibitadder_4_o), .i1({bitselector_6_out[10:0], {5{1'b0}}}), .o(xvibitadder_5_o));  // open: cIn, cOut
  BitSelector #(.width(16), .group(16)) bitselector_13 (.in(i0), .out(bitselector_13_out), .sel(not_1_out[12]));
  BitSelector #(.width(16), .group(16)) bitselector_14 (.in(i0), .out(bitselector_14_out), .sel(not_1_out[13]));
  BitSelector #(.width(16), .group(16)) bitselector_15 (.in(i0), .out(bitselector_15_out), .sel(not_1_out[14]));
  XVIbitAdder xvibitadder_6 (
    .i0(xvibitadder_5_o), .i1({bitselector_7_out[9:0], {6{1'b0}}}), .o(xvibitadder_6_o));  // open: cIn, cOut
  XVIbitAdder xvibitadder_7 (
    .i0(xvibitadder_6_o), .i1({bitselector_8_out[8:0], {7{1'b0}}}), .o(xvibitadder_7_o));  // open: cIn, cOut
  BitSelector #(.width(16), .group(16)) bitselector_16 (.in(i0), .out(bitselector_16_out), .sel(not_1_out[15]));
  XVIbitAdder xvibitadder_8 (
    .i0(xvibitadder_7_o), .i1({bitselector_9_out[7:0], {8{1'b0}}}), .o(xvibitadder_8_o));  // open: cIn, cOut
  XVIbitAdder xvibitadder_9 (
    .i0(xvibitadder_8_o), .i1({bitselector_10_out[6:0], {9{1'b0}}}), .o(xvibitadder_9_o));  // open: cIn, cOut
  XVIbitAdder xvibitadder_10 (
    .i0(xvibitadder_9_o), .i1({bitselector_11_out[5:0], {10{1'b0}}}), .o(xvibitadder_10_o));  // open: cIn, cOut
  XVIbitAdder xvibitadder_11 (
    .i0(xvibitadder_10_o), .i1({bitselector_12_out[4:0], {11{1'b0}}}), .o(xvibitadder_11_o));  // open: cIn, cOut
  XVIbitAdder xvibitadder_12 (
    .i0(xvibitadder_11_o), .i1({bitselector_13_out[3:0], {12{1'b0}}}), .o(xvibitadder_12_o));  // open: cIn, cOut
  XVIbitAdder xvibitadder_13 (
    .i0(xvibitadder_12_o), .i1({bitselector_14_out[2:0], {13{1'b0}}}), .o(xvibitadder_13_o));  // open: cIn, cOut
  XVIbitAdder xvibitadder_14 (
    .i0(xvibitadder_13_o), .i1({bitselector_15_out[1:0], {14{1'b0}}}), .o(xvibitadder_14_o));  // open: cIn, cOut
  XVIbitAdder xvibitadder_15 (
    .i0(xvibitadder_14_o), .i1({bitselector_16_out[0], {15{1'b0}}}), .o(o), .cOut(c));  // open: cIn
endmodule

module IVbitDecoder (
  input  [3:0] i,
  output [15:0] o
);

  wire not_1_out, not_2_out, not_3_out, not_4_out;

  and and_1 (o[0], not_1_out, not_2_out, not_3_out, not_4_out);
  not not_1 (not_1_out, i[0]);
  not not_2 (not_2_out, i[1]);
  not not_3 (not_3_out, i[2]);
  not not_4 (not_4_out, i[3]);
  and and_2 (o[1], i[0], not_2_out, not_3_out, not_4_out);
  and and_3 (o[2], not_1_out, i[1], not_3_out, not_4_out);
  and and_4 (o[3], i[0], i[1], not_3_out, not_4_out);
  and and_5 (o[4], not_1_out, not_2_out, i[2], not_4_out);
  and and_6 (o[5], i[0], not_2_out, i[2], not_4_out);
  and and_7 (o[7], i[0], i[1], i[2], not_4_out);
  and and_8 (o[6], not_1_out, i[1], i[2], not_4_out);
  and and_9 (o[8], not_1_out, not_2_out, not_3_out, i[3]);
  and and_10 (o[9], i[0], not_2_out, not_3_out, i[3]);
  and and_11 (o[10], not_1_out, i[1], not_3_out, i[3]);
  and and_12 (o[11], i[0], i[1], not_3_out, i[3]);
  and and_13 (o[12], not_1_out, not_2_out, i[2], i[3]);
  and and_14 (o[13], i[0], not_2_out, i[2], i[3]);
  and and_15 (o[14], not_1_out, i[1], i[2], i[3]);
  and and_16 (o[15], i[0], i[1], i[2], i[3]);
endmodule

module XVIbitDivisor (
  input  [15:0] dividend,
  input  [15:0] divisor,
  output [15:0] rest,
  output [15:0] quotient
);

  wire bitselector_1_out, bitselector_2_out, not_1_out, not_3_out, not_5_out, not_7_out, not_9_out,
       not_11_out, not_13_out, not_15_out, not_17_out, not_19_out, not_21_out, not_23_out, not_25_out,
       not_27_out, not_29_out, not_31_out, not_33_out, not_34_out, or_17_out, or_18_out,
       xvibitsoustractor_1_cout, xvibitsoustractor_2_cout, xvibitsoustractor_3_cout,
       xvibitsoustractor_4_cout, xvibitsoustractor_5_cout, xvibitsoustractor_6_cout,
       xvibitsoustractor_7_cout, xvibitsoustractor_8_cout, xvibitsoustractor_9_cout,
       xvibitsoustractor_10_cout, xvibitsoustractor_11_cout, xvibitsoustractor_12_cout,
       xvibitsoustractor_13_cout, xvibitsoustractor_14_cout, xvibitsoustractor_15_cout,
       xvibitsoustractor_16_cout;
  wire [1:0] bitselector_3_out, bitselector_4_out, or_2_out, xvibitnegtest_2_neg;
  wire [2:0] bitselector_5_out, bitselector_6_out, or_3_out;
  wire [3:0] bitselector_7_out, bitselector_8_out, iibitdecoder_1_o, or_4_out;
  wire [4:0] bitselector_9_out, bitselector_10_out, or_5_out;
  wire [5:0] bitselector_11_out, bitselector_12_out, or_6_out;
  wire [6:0] bitselector_13_out, bitselector_14_out, or_7_out;
  wire [7:0] bitselector_15_out, bitselector_16_out, or_8_out;
  wire [8:0] bitselector_17_out, bitselector_18_out, or_9_out;
  wire [9:0] bitselector_19_out, bitselector_20_out, or_10_out;
  wire [10:0] bitselector_21_out, bitselector_22_out, or_11_out;
  wire [11:0] bitselector_23_out, bitselector_24_out, or_12_out;
  wire [12:0] bitselector_25_out, bitselector_26_out, or_13_out, xvibitdoubleselector_1_o_2;
  wire [13:0] bitselector_27_out, bitselector_28_out, or_14_out;
  wire [14:0] bitselector_29_out, bitselector_30_out, or_15_out;
  wire [15:0] bitselector_31_out, bitselector_32_out, not_32_out, or_16_out, xvibitdoubleselector_2_o,
       xvibitinverter_1_o, xvibitinverter_2_o, xvibitinverter_3_o, xvibitinverter_4_o, xvibitnegtest_1_o,
       xvibitnegtest_2_o, xvibitsoustractor_1_o, xvibitsoustractor_2_o, xvibitsoustractor_3_o,
       xvibitsoustractor_4_o, xvibitsoustractor_5_o, xvibitsoustractor_6_o, xvibitsoustractor_7_o,
       xvibitsoustractor_8_o, xvibitsoustractor_9_o, xvibitsoustractor_10_o, xvibitsoustractor_11_o,
       xvibitsoustractor_12_o, xvibitsoustractor_13_o, xvibitsoustractor_14_o, xvibitsoustractor_15_o,
       xvibitsoustractor_16_o;
  wire [15:13] xvibitdoubleselector_1_o;
  wire [15:15] or_1_out;

  XVIbitNegTest xvibitnegtest_1 (.i(dividend), .o(xvibitnegtest_1_o), .neg(xvibitnegtest_2_neg[1]));
  XVIbitInverter xvibitinverter_1 (.i(xvibitnegtest_1_o), .o(xvibitinverter_1_o));  // open: cOut
  XVIbitNegTest xvibitnegtest_2 (.i(divisor), .o(xvibitnegtest_2_o), .neg(xvibitnegtest_2_neg[0]));
  XVIbitInverter xvibitinverter_2 (.i(xvibitnegtest_2_o), .o(xvibitinverter_2_o));  // open: cOut
  not not_1 (not_1_out, xvibitnegtest_2_neg[0]);
  XVIbitDoubleSelector xvibitdoubleselector_1 (
    .i0(dividend), .i1(xvibitinverter_1_o), .selector(xvibitnegtest_2_neg[1]),
    .o({xvibitdoubleselector_1_o, xvibitdoubleselector_1_o_2}));
  XVIbitDoubleSelector xvibitdoubleselector_2 (
    .i0(xvibitinverter_2_o), .i1(divisor), .selector(not_1_out), .o(xvibitdoubleselector_2_o));
  XVIbitSoustractor xvibitsoustractor_1 (
    .i0({{15{1'b0}}, xvibitdoubleselector_1_o[15]}), .i1(xvibitdoubleselector_2_o),
    .o(xvibitsoustractor_1_o), .cOut(xvibitsoustractor_1_cout));  // open: cIn
  not not_2 (not_32_out[15], xvibitsoustractor_1_cout);
  BitSelector #(.width(1)) bitselector_1 (.in(xvibitdoubleselector_1_o[15]), .out(bitselector_1_out), .sel(not_3_out));
  not not_3 (not_3_out, xvibitsoustractor_1_cout);
  BitSelector #(.width(1)) bitselector_2 (
    .in(xvibitsoustractor_1_o[0]), .out(bitselector_2_out), .sel(xvibitsoustractor_1_cout));
  or or_1 (or_1_out[15], bitselector_1_out, bitselector_2_out);
  not not_4 (not_32_out[14], xvibitsoustractor_2_cout);
  not not_5 (not_5_out, xvibitsoustractor_2_cout);
  XVIbitSoustractor xvibitsoustractor_2 (
    .i0({{14{1'b0}}, or_1_out[15], xvibitdoubleselector_1_o[14]}), .i1(xvibitdoubleselector_2_o),
    .o(xvibitsoustractor_2_o), .cOut(xvibitsoustractor_2_cout));  // open: cIn
  BitSelector #(.width(2), .group(2)) bitselector_3 (
    .in({or_1_out[15], xvibitdoubleselector_1_o[14]}), .out(bitselector_3_out), .sel(not_5_out));
  assign or_2_out = bitselector_3_out | bitselector_4_out;  // OR_Gate or_2, 2 bits wide
  BitSelector #(.width(2), .group(2)) bitselector_4 (
    .in(xvibitsoustractor_2_o[1:0]), .out(bitselector_4_out), .sel(xvibitsoustractor_2_cout));
  XVIbitSoustractor xvibitsoustractor_3 (
    .i0({{13{1'b0}}, or_2_out, xvibitdoubleselector_1_o[13]}), .i1(xvibitdoubleselector_2_o),
    .o(xvibitsoustractor_3_o), .cOut(xvibitsoustractor_3_cout));  // open: cIn
  not not_6 (not_32_out[13], xvibitsoustractor_3_cout);
  BitSelector #(.width(3), .group(3)) bitselector_5 (
    .in({or_2_out, xvibitdoubleselector_1_o[13]}), .out(bitselector_5_out), .sel(not_7_out));
  not not_7 (not_7_out, xvibitsoustractor_3_cout);
  BitSelector #(.width(3), .group(3)) bitselector_6 (
    .in(xvibitsoustractor_3_o[2:0]), .out(bitselector_6_out), .sel(xvibitsoustractor_3_cout));
  assign or_3_out = bitselector_5_out | bitselector_6_out;  // OR_Gate or_3, 3 bits wide
  XVIbitSoustractor xvibitsoustractor_4 (
    .i0({{12{1'b0}}, or_3_out, xvibitdoubleselector_1_o_2[12]}), .i1(xvibitdoubleselector_2_o),
    .o(xvibitsoustractor_4_o), .cOut(xvibitsoustractor_4_cout));  // open: cIn
  not not_8 (not_32_out[12], xvibitsoustractor_4_cout);
  BitSelector #(.width(4), .group(4)) bitselector_7 (
    .in({or_3_out, xvibitdoubleselector_1_o_2[12]}), .out(bitselector_7_out), .sel(not_9_out));
  not not_9 (not_9_out, xvibitsoustractor_4_cout);
  BitSelector #(.width(4), .group(4)) bitselector_8 (
    .in(xvibitsoustractor_4_o[3:0]), .out(bitselector_8_out), .sel(xvibitsoustractor_4_cout));
  assign or_4_out = bitselector_7_out | bitselector_8_out;  // OR_Gate or_4, 4 bits wide
  XVIbitSoustractor xvibitsoustractor_5 (
    .i0({{11{1'b0}}, or_4_out, xvibitdoubleselector_1_o_2[11]}), .i1(xvibitdoubleselector_2_o),
    .o(xvibitsoustractor_5_o), .cOut(xvibitsoustractor_5_cout));  // open: cIn
  not not_10 (not_32_out[11], xvibitsoustractor_5_cout);
  BitSelector #(.width(5), .group(5)) bitselector_9 (
    .in({or_4_out, xvibitdoubleselector_1_o_2[11]}), .out(bitselector_9_out), .sel(not_11_out));
  not not_11 (not_11_out, xvibitsoustractor_5_cout);
  BitSelector #(.width(5), .group(5)) bitselector_10 (
    .in(xvibitsoustractor_5_o[4:0]), .out(bitselector_10_out), .sel(xvibitsoustractor_5_cout));
  assign or_5_out = bitselector_9_out | bitselector_10_out;  // OR_Gate or_5, 5 bits wide
  not not_12 (not_32_out[10], xvibitsoustractor_6_cout);
  not not_13 (not_13_out, xvibitsoustractor_6_cout);
  XVIbitSoustractor xvibitsoustractor_6 (
    .i0({{10{1'b0}}, or_5_out, xvibitdoubleselector_1_o_2[10]}), .i1(xvibitdoubleselector_2_o),
    .o(xvibitsoustractor_6_o), .cOut(xvibitsoustractor_6_cout));  // open: cIn
  BitSelector #(.width(6), .group(6)) bitselector_11 (
    .in({or_5_out, xvibitdoubleselector_1_o_2[10]}), .out(bitselector_11_out), .sel(not_13_out));
  assign or_6_out = bitselector_11_out | bitselector_12_out;  // OR_Gate or_6, 6 bits wide
  BitSelector #(.width(6), .group(6)) bitselector_12 (
    .in(xvibitsoustractor_6_o[5:0]), .out(bitselector_12_out), .sel(xvibitsoustractor_6_cout));
  XVIbitSoustractor xvibitsoustractor_7 (
    .i0({{9{1'b0}}, or_6_out, xvibitdoubleselector_1_o_2[9]}), .i1(xvibitdoubleselector_2_o),
    .o(xvibitsoustractor_7_o), .cOut(xvibitsoustractor_7_cout));  // open: cIn
  not not_14 (not_32_out[9], xvibitsoustractor_7_cout);
  BitSelector #(.width(7), .group(7)) bitselector_13 (
    .in({or_6_out, xvibitdoubleselector_1_o_2[9]}), .out(bitselector_13_out), .sel(not_15_out));
  not not_15 (not_15_out, xvibitsoustractor_7_cout);
  BitSelector #(.width(7), .group(7)) bitselector_14 (
    .in(xvibitsoustractor_7_o[6:0]), .out(bitselector_14_out), .sel(xvibitsoustractor_7_cout));
  assign or_7_out = bitselector_13_out | bitselector_14_out;  // OR_Gate or_7, 7 bits wide
  XVIbitSoustractor xvibitsoustractor_8 (
    .i0({{8{1'b0}}, or_7_out, xvibitdoubleselector_1_o_2[8]}), .i1(xvibitdoubleselector_2_o),
    .o(xvibitsoustractor_8_o), .cOut(xvibitsoustractor_8_cout));  // open: cIn
  not not_16 (not_32_out[8], xvibitsoustractor_8_cout);
  BitSelector #(.group(8)) bitselector_15 (
    .in({or_7_out, xvibitdoubleselector_1_o_2[8]}), .out(bitselector_15_out), .sel(not_17_out));
  not not_17 (not_17_out, xvibitsoustractor_8_cout);
  BitSelector #(.group(8)) bitselector_16 (
    .in(xvibitsoustractor_8_o[7:0]), .out(bitselector_16_out), .sel(xvibitsoustractor_8_cout));
  assign or_8_out = bitselector_15_out | bitselector_16_out;  // OR_Gate or_8, 8 bits wide
  XVIbitSoustractor xvibitsoustractor_9 (
    .i0({{7{1'b0}}, or_8_out, xvibitdoubleselector_1_o_2[7]}), .i1(xvibitdoubleselector_2_o),
    .o(xvibitsoustractor_9_o), .cOut(xvibitsoustractor_9_cout));  // open: cIn
  not not_18 (not_32_out[7], xvibitsoustractor_9_cout);
  BitSelector #(.width(9), .group(9)) bitselector_17 (
    .in({or_8_out, xvibitdoubleselector_1_o_2[7]}), .out(bitselector_17_out), .sel(not_19_out));
  not not_19 (not_19_out, xvibitsoustractor_9_cout);
  BitSelector #(.width(9), .group(9)) bitselector_18 (
    .in(xvibitsoustractor_9_o[8:0]), .out(bitselector_18_out), .sel(xvibitsoustractor_9_cout));
  assign or_9_out = bitselector_17_out | bitselector_18_out;  // OR_Gate or_9, 9 bits wide
  not not_20 (not_32_out[6], xvibitsoustractor_10_cout);
  not not_21 (not_21_out, xvibitsoustractor_10_cout);
  XVIbitSoustractor xvibitsoustractor_10 (
    .i0({{6{1'b0}}, or_9_out, xvibitdoubleselector_1_o_2[6]}), .i1(xvibitdoubleselector_2_o),
    .o(xvibitsoustractor_10_o), .cOut(xvibitsoustractor_10_cout));  // open: cIn
  BitSelector #(.width(10), .group(10)) bitselector_19 (
    .in({or_9_out, xvibitdoubleselector_1_o_2[6]}), .out(bitselector_19_out), .sel(not_21_out));
  assign or_10_out = bitselector_19_out | bitselector_20_out;  // OR_Gate or_10, 10 bits wide
  BitSelector #(.width(10), .group(10)) bitselector_20 (
    .in(xvibitsoustractor_10_o[9:0]), .out(bitselector_20_out), .sel(xvibitsoustractor_10_cout));
  XVIbitSoustractor xvibitsoustractor_11 (
    .i0({{5{1'b0}}, or_10_out, xvibitdoubleselector_1_o_2[5]}), .i1(xvibitdoubleselector_2_o),
    .o(xvibitsoustractor_11_o), .cOut(xvibitsoustractor_11_cout));  // open: cIn
  not not_22 (not_32_out[5], xvibitsoustractor_11_cout);
  BitSelector #(.width(11), .group(11)) bitselector_21 (
    .in({or_10_out, xvibitdoubleselector_1_o_2[5]}), .out(bitselector_21_out), .sel(not_23_out));
  not not_23 (not_23_out, xvibitsoustractor_11_cout);
  BitSelector #(.width(11), .group(11)) bitselector_22 (
    .in(xvibitsoustractor_11_o[10:0]), .out(bitselector_22_out), .sel(xvibitsoustractor_11_cout));
  assign or_11_out = bitselector_21_out | bitselector_22_out;  // OR_Gate or_11, 11 bits wide
  XVIbitSoustractor xvibitsoustractor_12 (
    .i0({4'b0000, or_11_out, xvibitdoubleselector_1_o_2[4]}), .i1(xvibitdoubleselector_2_o),
    .o(xvibitsoustractor_12_o), .cOut(xvibitsoustractor_12_cout));  // open: cIn
  not not_24 (not_32_out[4], xvibitsoustractor_12_cout);
  BitSelector #(.width(12), .group(12)) bitselector_23 (
    .in({or_11_out, xvibitdoubleselector_1_o_2[4]}), .out(bitselector_23_out), .sel(not_25_out));
  not not_25 (not_25_out, xvibitsoustractor_12_cout);
  BitSelector #(.width(12), .group(12)) bitselector_24 (
    .in(xvibitsoustractor_12_o[11:0]), .out(bitselector_24_out), .sel(xvibitsoustractor_12_cout));
  assign or_12_out = bitselector_23_out | bitselector_24_out;  // OR_Gate or_12, 12 bits wide
  XVIbitSoustractor xvibitsoustractor_13 (
    .i0({3'b000, or_12_out, xvibitdoubleselector_1_o_2[3]}), .i1(xvibitdoubleselector_2_o),
    .o(xvibitsoustractor_13_o), .cOut(xvibitsoustractor_13_cout));  // open: cIn
  not not_26 (not_32_out[3], xvibitsoustractor_13_cout);
  BitSelector #(.width(13), .group(13)) bitselector_25 (
    .in({or_12_out, xvibitdoubleselector_1_o_2[3]}), .out(bitselector_25_out), .sel(not_27_out));
  not not_27 (not_27_out, xvibitsoustractor_13_cout);
  BitSelector #(.width(13), .group(13)) bitselector_26 (
    .in(xvibitsoustractor_13_o[12:0]), .out(bitselector_26_out), .sel(xvibitsoustractor_13_cout));
  assign or_13_out = bitselector_25_out | bitselector_26_out;  // OR_Gate or_13, 13 bits wide
  not not_28 (not_32_out[2], xvibitsoustractor_14_cout);
  not not_29 (not_29_out, xvibitsoustractor_14_cout);
  XVIbitSoustractor xvibitsoustractor_14 (
    .i0({2'b00, or_13_out, xvibitdoubleselector_1_o_2[2]}), .i1(xvibitdoubleselector_2_o),
    .o(xvibitsoustractor_14_o), .cOut(xvibitsoustractor_14_cout));  // open: cIn
  BitSelector #(.width(14), .group(14)) bitselector_27 (
    .in({or_13_out, xvibitdoubleselector_1_o_2[2]}), .out(bitselector_27_out), .sel(not_29_out));
  assign or_14_out = bitselector_27_out | bitselector_28_out;  // OR_Gate or_14, 14 bits wide
  BitSelector #(.width(14), .group(14)) bitselector_28 (
    .in(xvibitsoustractor_14_o[13:0]), .out(bitselector_28_out), .sel(xvibitsoustractor_14_cout));
  XVIbitSoustractor xvibitsoustractor_15 (
    .i0({1'b0, or_14_out, xvibitdoubleselector_1_o_2[1]}), .i1(xvibitdoubleselector_2_o),
    .o(xvibitsoustractor_15_o), .cOut(xvibitsoustractor_15_cout));  // open: cIn
  not not_30 (not_32_out[1], xvibitsoustractor_15_cout);
  BitSelector #(.width(15), .group(15)) bitselector_29 (
    .in({or_14_out, xvibitdoubleselector_1_o_2[1]}), .out(bitselector_29_out), .sel(not_31_out));
  not not_31 (not_31_out, xvibitsoustractor_15_cout);
  BitSelector #(.width(15), .group(15)) bitselector_30 (
    .in(xvibitsoustractor_15_o[14:0]), .out(bitselector_30_out), .sel(xvibitsoustractor_15_cout));
  assign or_15_out = bitselector_29_out | bitselector_30_out;  // OR_Gate or_15, 15 bits wide
  not not_32 (not_32_out[0], xvibitsoustractor_16_cout);
  BitSelector #(.width(16), .group(16)) bitselector_31 (
    .in({or_15_out, xvibitdoubleselector_1_o_2[0]}), .out(bitselector_31_out), .sel(not_33_out));
  not not_33 (not_33_out, xvibitsoustractor_16_cout);
  XVIbitSoustractor xvibitsoustractor_16 (
    .i0({or_15_out, xvibitdoubleselector_1_o_2[0]}), .i1(xvibitdoubleselector_2_o),
    .o(xvibitsoustractor_16_o), .cOut(xvibitsoustractor_16_cout));  // open: cIn
  BitSelector #(.width(16), .group(16)) bitselector_32 (
    .in(xvibitsoustractor_16_o), .out(bitselector_32_out), .sel(xvibitsoustractor_16_cout));
  assign or_16_out = bitselector_31_out | bitselector_32_out;  // OR_Gate or_16, 16 bits wide
  IIbitDecoder iibitdecoder_1 (.i(xvibitnegtest_2_neg), .o(iibitdecoder_1_o));
  XVIbitDoubleSelector xvibitdoubleselector_3 (.i0(or_16_out), .i1(xvibitinverter_3_o), .selector(or_17_out), .o(rest));
  XVIbitInverter xvibitinverter_3 (.i(or_16_out), .o(xvibitinverter_3_o));  // open: cOut
  XVIbitInverter xvibitinverter_4 (.i(not_32_out), .o(xvibitinverter_4_o));  // open: cOut
  XVIbitDoubleSelector xvibitdoubleselector_4 (
    .i0(xvibitinverter_4_o), .i1(not_32_out), .selector(not_34_out), .o(quotient));
  or or_17 (or_17_out, iibitdecoder_1_o[3], iibitdecoder_1_o[2]);
  not not_34 (not_34_out, or_18_out);
  or or_18 (or_18_out, iibitdecoder_1_o[1], iibitdecoder_1_o[2]);

  // Notes on the sheet:
  //   divisor sign
  //   dividend sign
endmodule

module XVIbitNegTest (
  input  [15:0] i,
  output [15:0] o,
  output neg
);


  assign neg = i[15];
  assign o = i;
endmodule

module XVIbitDoubleSelector (
  input  [15:0] i0,
  input  [15:0] i1,
  input  selector,
  output [15:0] o
);

  wire not_1_out;
  wire [15:0] bitselector_1_out, bitselector_2_out;

  BitSelector #(.width(16), .group(16)) bitselector_1 (.in(i0), .out(bitselector_1_out), .sel(selector));
  BitSelector #(.width(16), .group(16)) bitselector_2 (.in(i1), .out(bitselector_2_out), .sel(not_1_out));
  not not_1 (not_1_out, selector);
  assign o = bitselector_1_out | bitselector_2_out;  // OR_Gate or_1, 16 bits wide
endmodule

module IIbitDecoder (
  input  [1:0] i,
  output [3:0] o
);

  wire not_1_out, not_2_out;

  not not_1 (not_1_out, i[0]);
  not not_2 (not_2_out, i[1]);
  and and_1 (o[1], i[0], not_2_out);
  and and_2 (o[0], not_1_out, not_2_out);
  and and_3 (o[3], i[0], i[1]);
  and and_4 (o[2], not_1_out, i[1]);
endmodule

module XVIbitSignedSoustractor (
  input  cIn,
  input  [15:0] i0,
  input  [15:0] i1,
  output [15:0] o,
  output cOut
);

  wire xvibitadder_1_cout, xvibitnegtest_1_neg, xvibitsoustractor_1_cout;
  wire [15:0] xvibitadder_1_o, xvibitinverter_1_o, xvibitnegtest_1_o, xvibitsoustractor_1_o;

  XVIbitNegTest xvibitnegtest_1 (.i(i1), .o(xvibitnegtest_1_o), .neg(xvibitnegtest_1_neg));
  XVIbitInverter xvibitinverter_1 (.i(xvibitnegtest_1_o), .o(xvibitinverter_1_o));  // open: cOut
  XVIbitSoustractor xvibitsoustractor_1 (
    .cIn(cIn), .i0(i0), .i1(xvibitnegtest_1_o), .o(xvibitsoustractor_1_o), .cOut(xvibitsoustractor_1_cout));
  XVIbitDoubleSelector xvibitdoubleselector_1 (
    .i0(xvibitsoustractor_1_o), .i1(xvibitadder_1_o), .selector(xvibitnegtest_1_neg), .o(o));
  XVIbitAdder xvibitadder_1 (
    .cIn(cIn), .i0(i0), .i1(xvibitinverter_1_o), .o(xvibitadder_1_o), .cOut(xvibitadder_1_cout));
  IIbitDoubleSelector iibitdoubleselector_1 (
    .i0(xvibitsoustractor_1_cout), .i1(xvibitadder_1_cout), .o(cOut), .selector(xvibitnegtest_1_neg));
endmodule

module IIbitDoubleSelector (
  input  i0,
  input  i1,
  input  selector,
  output o
);

  wire bitselector_1_out, bitselector_2_out, not_1_out;

  BitSelector #(.width(1)) bitselector_1 (.in(i0), .out(bitselector_1_out), .sel(selector));
  BitSelector #(.width(1)) bitselector_2 (.in(i1), .out(bitselector_2_out), .sel(not_1_out));
  not not_1 (not_1_out, selector);
  or or_1 (o, bitselector_1_out, bitselector_2_out);
endmodule

module IIIbitDecoder (
  input  [2:0] i,
  output [7:0] o
);

  wire not_1_out, not_2_out, not_3_out;

  not not_1 (not_1_out, i[0]);
  not not_2 (not_2_out, i[1]);
  not not_3 (not_3_out, i[2]);
  and and_1 (o[0], not_1_out, not_2_out, not_3_out);
  and and_2 (o[1], i[0], not_2_out, not_3_out);
  and and_3 (o[3], i[0], i[1], not_3_out);
  and and_4 (o[2], not_1_out, i[1], not_3_out);
  and and_5 (o[5], i[0], not_2_out, i[2]);
  and and_6 (o[4], not_1_out, not_2_out, i[2]);
  and and_7 (o[6], not_1_out, i[1], i[2]);
  and and_8 (o[7], i[0], i[1], i[2]);
endmodule

module IIIbitEncoder (
  input  [7:0] in_1,
  output [2:0] o
);

  wire or_1_out, or_2_out, or_3_out, or_4_out, or_5_out, or_6_out, or_7_out, or_8_out, or_9_out, or_10_out,
       or_11_out, or_12_out, or_13_out, or_14_out, or_15_out, or_16_out, or_17_out, or_18_out;

  or or_1 (or_1_out, 1'b0, in_1[1]);
  buf or_2 (or_2_out, 1'b0);  // OR_Gate
  buf or_3 (or_3_out, 1'b0);  // OR_Gate
  buf or_4 (or_4_out, or_1_out);  // OR_Gate
  or or_5 (or_5_out, or_2_out, in_1[2]);
  buf or_6 (or_6_out, or_3_out);  // OR_Gate
  or or_7 (or_7_out, or_4_out, in_1[3]);
  or or_8 (or_8_out, or_5_out, in_1[3]);
  buf or_9 (or_9_out, or_6_out);  // OR_Gate
  buf or_10 (or_10_out, or_7_out);  // OR_Gate
  buf or_11 (or_11_out, or_8_out);  // OR_Gate
  or or_12 (or_12_out, or_9_out, in_1[4]);
  or or_13 (or_13_out, or_10_out, in_1[5]);
  buf or_14 (or_14_out, or_11_out);  // OR_Gate
  or or_15 (or_15_out, or_12_out, in_1[5]);
  buf or_16 (or_16_out, or_13_out);  // OR_Gate
  or or_17 (or_17_out, or_14_out, in_1[6]);
  or or_18 (or_18_out, or_15_out, in_1[6]);
  or or_19 (o[0], or_16_out, in_1[7]);
  or or_20 (o[1], or_17_out, in_1[7]);
  or or_21 (o[2], or_18_out, in_1[7]);
endmodule

module ItoIVdemultiplexor (
  input  [7:0] selector,
  input  [15:0] i,
  output [15:0] o0,
  output [15:0] o1,
  output [15:0] o2,
  output [15:0] o3,
  output [15:0] o4,
  output [15:0] o5,
  output [15:0] o6,
  output [15:0] o7
);

  wire [7:0] not_1_out;

  assign not_1_out = ~selector;  // NOT_Gate not_1, 8 bits wide
  BitSelector #(.width(16), .group(16)) bitselector_1 (.in(i), .out(o0), .sel(not_1_out[0]));
  BitSelector #(.width(16), .group(16)) bitselector_2 (.in(i), .out(o1), .sel(not_1_out[1]));
  BitSelector #(.width(16), .group(16)) bitselector_3 (.in(i), .out(o2), .sel(not_1_out[2]));
  BitSelector #(.width(16), .group(16)) bitselector_4 (.in(i), .out(o3), .sel(not_1_out[3]));
  BitSelector #(.width(16), .group(16)) bitselector_5 (.in(i), .out(o4), .sel(not_1_out[4]));
  BitSelector #(.width(16), .group(16)) bitselector_6 (.in(i), .out(o5), .sel(not_1_out[5]));
  BitSelector #(.width(16), .group(16)) bitselector_7 (.in(i), .out(o6), .sel(not_1_out[6]));
  BitSelector #(.width(16), .group(16)) bitselector_8 (.in(i), .out(o7), .sel(not_1_out[7]));
endmodule

module VIIItoImultiplexor (
  input  [7:0] selector,
  input  [15:0] i0,
  input  [15:0] i1,
  input  [15:0] i2,
  input  [15:0] i3,
  input  [15:0] i4,
  input  [15:0] i5,
  input  [15:0] i6,
  input  [15:0] i7,
  output [15:0] o
);

  wire [7:0] not_1_out;
  wire [15:0] bitselector_1_out, bitselector_2_out, bitselector_3_out, bitselector_4_out, bitselector_5_out,
       bitselector_6_out, bitselector_7_out, bitselector_8_out;

  assign not_1_out = ~selector;  // NOT_Gate not_1, 8 bits wide
  BitSelector #(.width(16), .group(16)) bitselector_1 (.in(i0), .out(bitselector_1_out), .sel(not_1_out[0]));
  BitSelector #(.width(16), .group(16)) bitselector_2 (.in(i1), .out(bitselector_2_out), .sel(not_1_out[1]));
  BitSelector #(.width(16), .group(16)) bitselector_3 (.in(i2), .out(bitselector_3_out), .sel(not_1_out[2]));
  BitSelector #(.width(16), .group(16)) bitselector_4 (.in(i3), .out(bitselector_4_out), .sel(not_1_out[3]));
  BitSelector #(.width(16), .group(16)) bitselector_5 (.in(i4), .out(bitselector_5_out), .sel(not_1_out[4]));
  BitSelector #(.width(16), .group(16)) bitselector_6 (.in(i5), .out(bitselector_6_out), .sel(not_1_out[5]));
  BitSelector #(.width(16), .group(16)) bitselector_7 (.in(i6), .out(bitselector_7_out), .sel(not_1_out[6]));
  BitSelector #(.width(16), .group(16)) bitselector_8 (.in(i7), .out(bitselector_8_out), .sel(not_1_out[7]));
  assign o = bitselector_1_out | bitselector_2_out | bitselector_3_out | bitselector_4_out | bitselector_5_out | bitselector_6_out | bitselector_7_out | bitselector_8_out;  // OR_Gate or_1, 16 bits wide
endmodule

module ALU (
  input  [2:0] operation,
  input  [15:0] i0,
  input  [15:0] i1,
  output [15:0] o,
  output equalFlag,
  output greaterFlag,
  output lesserFlag,
  output zeroFlag,
  output rSignFlag,
  output overflowFlag,
  output underflowFlag
);

  wire comparisoncheks_1_equal, comparisoncheks_1_greater, comparisoncheks_1_i0sign,
       comparisoncheks_1_i1sign, comparisoncheks_1_lesser, not_1_out, or_1_out, or_6_out, xvibitnegtest_1_neg;
  wire [7:0] iiibitdecoder_1_o;
  wire [15:0] comparisoncheks_1_o, iitoimultiplexor_1_o, itoivdemultiplexor_1_o0, itoivdemultiplexor_1_o2,
       itoivdemultiplexor_1_o3, itoivdemultiplexor_1_o4, itoivdemultiplexor_1_o5, itoivdemultiplexor_2_o0,
       itoivdemultiplexor_2_o2, itoivdemultiplexor_2_o3, itoivdemultiplexor_2_o4, itoivdemultiplexor_2_o5,
       or_2_out, or_3_out, or_4_out, or_5_out, viiitoimultiplexor_1_o, xvibitadder_1_o,
       xvibitdivisor_1_quotient, xvibitdivisor_1_rest, xvibitmutliplicator_1_o;

  IIIbitDecoder iiibitdecoder_1 (.i(operation), .o(iiibitdecoder_1_o));
  IItoIMultiplexor iitoimultiplexor_1 (.i0(i1), .i1(16'h1), .o(iitoimultiplexor_1_o), .selector(or_1_out));
  or or_1 (or_1_out, iiibitdecoder_1_o[5], iiibitdecoder_1_o[6]);
  ItoIVdemultiplexor itoivdemultiplexor_1 (
    .selector(iiibitdecoder_1_o), .i(i0), .o0(itoivdemultiplexor_1_o0), .o2(itoivdemultiplexor_1_o2),
    .o3(itoivdemultiplexor_1_o3), .o4(itoivdemultiplexor_1_o4), .o5(itoivdemultiplexor_1_o5));  // open: o1, o6, o7
  ItoIVdemultiplexor itoivdemultiplexor_2 (
    .selector(iiibitdecoder_1_o), .i(iitoimultiplexor_1_o), .o0(itoivdemultiplexor_2_o0),
    .o2(itoivdemultiplexor_2_o2), .o3(itoivdemultiplexor_2_o3), .o4(itoivdemultiplexor_2_o4),
    .o5(itoivdemultiplexor_2_o5));  // open: o1, o6, o7
  comparisonCheks comparisoncheks_1 (
    .i0(i0), .i1(iitoimultiplexor_1_o), .o(comparisoncheks_1_o), .i0Sign(comparisoncheks_1_i0sign),
    .i1Sign(comparisoncheks_1_i1sign), .lesser(comparisoncheks_1_lesser),
    .greater(comparisoncheks_1_greater), .equal(comparisoncheks_1_equal));
  assign or_2_out = itoivdemultiplexor_1_o0 | itoivdemultiplexor_1_o5;  // OR_Gate or_2, 16 bits wide
  assign or_3_out = itoivdemultiplexor_2_o0 | itoivdemultiplexor_2_o5;  // OR_Gate or_3, 16 bits wide
  assign or_4_out = itoivdemultiplexor_1_o3 | itoivdemultiplexor_1_o4;  // OR_Gate or_4, 16 bits wide
  assign or_5_out = itoivdemultiplexor_2_o3 | itoivdemultiplexor_2_o4;  // OR_Gate or_5, 16 bits wide
  XVIbitAdder xvibitadder_1 (.i0(or_2_out), .i1(or_3_out), .o(xvibitadder_1_o));  // open: cIn, cOut
  XVIbitMutliplicator xvibitmutliplicator_1 (
    .i0(itoivdemultiplexor_1_o2), .o(xvibitmutliplicator_1_o), .i1(itoivdemultiplexor_2_o2));  // open: c
  XVIbitDivisor xvibitdivisor_1 (
    .dividend(or_4_out), .rest(xvibitdivisor_1_rest), .divisor(or_5_out), .quotient(xvibitdivisor_1_quotient));
  VIIItoImultiplexor viiitoimultiplexor_1 (
    .selector(iiibitdecoder_1_o), .i0(xvibitadder_1_o), .i1(comparisoncheks_1_o),
    .i2(xvibitmutliplicator_1_o), .i3(xvibitdivisor_1_quotient), .i4(xvibitdivisor_1_rest),
    .i5(xvibitadder_1_o), .i6(comparisoncheks_1_o), .o(viiitoimultiplexor_1_o));  // open: i7
  XVIbitNegTest xvibitnegtest_1 (.i(viiitoimultiplexor_1_o), .o(o), .neg(xvibitnegtest_1_neg));
  flags flags_1 (
    .operation(iiibitdecoder_1_o), .equal_2(equalFlag), .greater_2(greaterFlag), .lesser_2(lesserFlag),
    .zero_2(zeroFlag), .resultSign_2(rSignFlag), .overflow(overflowFlag), .underflow(underflowFlag),
    .i0Sign(comparisoncheks_1_i0sign), .i1Sign(comparisoncheks_1_i1sign), .resultSign(xvibitnegtest_1_neg),
    .zero(not_1_out), .lesser(comparisoncheks_1_lesser), .greater(comparisoncheks_1_greater),
    .equal(comparisoncheks_1_equal));
  or or_6 (or_6_out, o[15], o[14], o[13], o[12], o[11], o[10], o[9], o[8], o[7], o[6], o[5], o[4], o[3], o[2], o[1], o[0]);
  not not_1 (not_1_out, or_6_out);

  // Notes on the sheet:
  //   0 = addition
  //   1 = soustraction
  //   2 = multiplication
  //   3 = division
  //   4 = modulo
  //   5 = increment
  //   6 = decrement
  //   does the soustraction as well
endmodule

module flags (
  input  i0Sign,
  input  i1Sign,
  input  resultSign,
  input  zero,
  input  lesser,
  input  greater,
  input  equal,
  input  [7:0] operation,
  output equal_2,
  output greater_2,
  output lesser_2,
  output zero_2,
  output resultSign_2,
  output overflow,
  output underflow
);

  wire and_1_out, and_2_out, and_3_out, and_4_out, and_5_out, and_6_out, and_7_out, and_8_out, and_9_out,
       and_10_out, not_1_out, not_2_out, not_3_out, not_4_out, not_5_out, not_6_out, not_7_out, or_1_out,
       or_2_out, or_3_out, or_4_out;

  not not_1 (not_1_out, i0Sign);
  and and_1 (and_1_out, not_1_out, not_2_out);
  or or_1 (or_1_out, operation[0], operation[5]);
  or or_2 (or_2_out, operation[1], operation[6]);
  not not_2 (not_2_out, i1Sign);
  and and_2 (and_2_out, i0Sign, i1Sign);
  and and_3 (and_3_out, i0Sign, not_4_out);
  not not_3 (not_3_out, i0Sign);
  not not_4 (not_4_out, i1Sign);
  and and_4 (and_4_out, not_3_out, i1Sign);
  or or_3 (or_3_out, and_2_out, and_1_out);
  or or_4 (or_4_out, and_4_out, and_3_out);
  and and_5 (and_5_out, resultSign, and_1_out, or_1_out);
  not not_5 (not_5_out, resultSign);
  and and_6 (and_6_out, not_5_out, and_2_out, or_1_out);
  and and_7 (and_7_out, resultSign, and_4_out, or_2_out);
  not not_6 (not_6_out, resultSign);
  and and_8 (and_8_out, not_6_out, and_3_out, or_2_out);
  and and_9 (and_9_out, resultSign, or_3_out, operation[2]);
  not not_7 (not_7_out, resultSign);
  and and_10 (and_10_out, not_7_out, or_4_out, operation[2]);
  or or_5 (overflow, and_5_out, and_7_out, and_9_out);
  or or_6 (underflow, and_6_out, and_8_out, and_10_out);

  assign equal_2 = equal;
  assign greater_2 = greater;
  assign lesser_2 = lesser;
  assign resultSign_2 = resultSign;
  assign zero_2 = zero;

  // Notes on the sheet:
  //   0 = addition
  //   1 = soustraction
  //   2 = multiplication
  //   3 = division
  //   4 = modulo
  //   5 = increment
  //   6 = decrement
endmodule

module IItoIMultiplexor (
  input  [15:0] i0,
  input  [15:0] i1,
  input  selector,
  output [15:0] o
);

  wire not_1_out;
  wire [15:0] bitselector_1_out, bitselector_2_out;

  BitSelector #(.width(16), .group(16)) bitselector_1 (.in(i0), .out(bitselector_1_out), .sel(selector));
  BitSelector #(.width(16), .group(16)) bitselector_2 (.in(i1), .out(bitselector_2_out), .sel(not_1_out));
  not not_1 (not_1_out, selector);
  assign o = bitselector_1_out | bitselector_2_out;  // OR_Gate or_1, 16 bits wide
endmodule

module fullComparisonChecks (
  input  [15:0] i0,
  input  [15:0] i1,
  output [15:0] o,
  output lesser,
  output greater,
  output equal,
  output [15:0] absO,
  output i0Sign,
  output i1Sign,
  output absLesser,
  output absGreater,
  output absEqual
);

  wire or_1_out, or_2_out, or_3_out, or_4_out;
  wire [15:0] iitoimultiplexor_1_o, iitoimultiplexor_2_o, xvibitinverter_1_o, xvibitinverter_2_o,
       xvibitnegtest_1_o, xvibitnegtest_2_o, xvibitsignedsoustractor_1_o, xvibitsoustractor_1_o;

  XVIbitNegTest xvibitnegtest_1 (.i(i0), .o(xvibitnegtest_1_o), .neg(i0Sign));
  XVIbitNegTest xvibitnegtest_2 (.i(i1), .o(xvibitnegtest_2_o), .neg(i1Sign));
  XVIbitInverter xvibitinverter_1 (.i(xvibitnegtest_1_o), .o(xvibitinverter_1_o));  // open: cOut
  XVIbitInverter xvibitinverter_2 (.i(xvibitnegtest_2_o), .o(xvibitinverter_2_o));  // open: cOut
  IItoIMultiplexor iitoimultiplexor_1 (
    .i0(xvibitnegtest_1_o), .i1(xvibitinverter_1_o), .o(iitoimultiplexor_1_o), .selector(i0Sign));
  IItoIMultiplexor iitoimultiplexor_2 (
    .i0(xvibitnegtest_2_o), .i1(xvibitinverter_2_o), .o(iitoimultiplexor_2_o), .selector(i1Sign));
  XVIbitSignedSoustractor xvibitsignedsoustractor_1 (
    .i0(xvibitnegtest_1_o), .i1(xvibitnegtest_2_o), .o(xvibitsignedsoustractor_1_o));  // open: cIn, cOut
  XVIbitSoustractor xvibitsoustractor_1 (
    .i0(iitoimultiplexor_1_o), .i1(iitoimultiplexor_2_o), .o(xvibitsoustractor_1_o));  // open: cIn, cOut
  XVIbitNegTest xvibitnegtest_3 (.i(xvibitsignedsoustractor_1_o), .o(o), .neg(lesser));
  or or_1 (or_1_out, lesser, equal);
  not not_1 (greater, or_1_out);
  XVIbitNegTest xvibitnegtest_4 (.i(xvibitsoustractor_1_o), .o(absO), .neg(absLesser));
  or or_2 (or_2_out, absLesser, absEqual);
  not not_2 (absGreater, or_2_out);
  or or_3 (or_3_out, o[15], o[14], o[13], o[12], o[11], o[10], o[9], o[8], o[7], o[6], o[5], o[4], o[3], o[2], o[1], o[0]);
  not not_3 (equal, or_3_out);
  or or_4 (or_4_out, absO[15], absO[14], absO[13], absO[12], absO[11], absO[10], absO[9], absO[8], absO[7], absO[6], absO[5], absO[4], absO[3], absO[2], absO[1], absO[0]);
  not not_4 (absEqual, or_4_out);
endmodule

module comparisonCheks (
  input  [15:0] i0,
  input  [15:0] i1,
  output [15:0] o,
  output i0Sign,
  output i1Sign,
  output lesser,
  output greater,
  output equal
);

  wire or_1_out, or_2_out;
  wire [15:0] xvibitnegtest_1_o, xvibitnegtest_2_o, xvibitsignedsoustractor_1_o;

  XVIbitNegTest xvibitnegtest_1 (.i(i0), .o(xvibitnegtest_1_o), .neg(i0Sign));
  XVIbitNegTest xvibitnegtest_2 (.i(i1), .o(xvibitnegtest_2_o), .neg(i1Sign));
  XVIbitSignedSoustractor xvibitsignedsoustractor_1 (
    .i0(xvibitnegtest_1_o), .i1(xvibitnegtest_2_o), .o(xvibitsignedsoustractor_1_o));  // open: cIn, cOut
  XVIbitNegTest xvibitnegtest_3 (.i(xvibitsignedsoustractor_1_o), .o(o), .neg(lesser));
  or or_1 (or_1_out, lesser, equal);
  not not_1 (greater, or_1_out);
  or or_2 (or_2_out, o[15], o[14], o[13], o[12], o[11], o[10], o[9], o[8], o[7], o[6], o[5], o[4], o[3], o[2], o[1], o[0]);
  not not_2 (equal, or_2_out);
endmodule

module register (
  input  [15:0] data,
  input  write,
  input  clock,
  output [15:0] dataO
);

  bitMemCell bitmemcell_1 (.data(data[3]), .write(write), .clock(clock), .out(dataO[3]));  // open: nOut, set, reset
  bitMemCell bitmemcell_2 (.data(data[7]), .write(write), .clock(clock), .out(dataO[7]));  // open: nOut, set, reset
  bitMemCell bitmemcell_3 (.data(data[11]), .write(write), .clock(clock), .out(dataO[11]));  // open: nOut, set, reset
  bitMemCell bitmemcell_4 (.data(data[15]), .write(write), .clock(clock), .out(dataO[15]));  // open: nOut, set, reset
  bitMemCell bitmemcell_5 (.data(data[2]), .write(write), .clock(clock), .out(dataO[2]));  // open: nOut, set, reset
  bitMemCell bitmemcell_6 (.data(data[6]), .write(write), .clock(clock), .out(dataO[6]));  // open: nOut, set, reset
  bitMemCell bitmemcell_7 (.data(data[10]), .write(write), .clock(clock), .out(dataO[10]));  // open: nOut, set, reset
  bitMemCell bitmemcell_8 (.data(data[14]), .write(write), .clock(clock), .out(dataO[14]));  // open: nOut, set, reset
  bitMemCell bitmemcell_9 (.data(data[1]), .write(write), .clock(clock), .out(dataO[1]));  // open: nOut, set, reset
  bitMemCell bitmemcell_10 (.data(data[5]), .write(write), .clock(clock), .out(dataO[5]));  // open: nOut, set, reset
  bitMemCell bitmemcell_11 (.data(data[9]), .write(write), .clock(clock), .out(dataO[9]));  // open: nOut, set, reset
  bitMemCell bitmemcell_12 (.data(data[13]), .write(write), .clock(clock), .out(dataO[13]));  // open: nOut, set, reset
  bitMemCell bitmemcell_13 (.data(data[0]), .write(write), .clock(clock), .out(dataO[0]));  // open: nOut, set, reset
  bitMemCell bitmemcell_14 (.data(data[4]), .write(write), .clock(clock), .out(dataO[4]));  // open: nOut, set, reset
  bitMemCell bitmemcell_15 (.data(data[8]), .write(write), .clock(clock), .out(dataO[8]));  // open: nOut, set, reset
  bitMemCell bitmemcell_16 (.data(data[12]), .write(write), .clock(clock), .out(dataO[12]));  // open: nOut, set, reset
endmodule

module bitMemCell (
  input  set,
  input  data,
  input  write,
  input  clock,
  input  reset,
  output out,
  output nOut
);

  wire and_1_out;

  and and_1 (and_1_out, write, clock);
  D_Flip_Flop d_ff_1 (.D(data), .clk(and_1_out), .Q(out), .Qn(nOut), .preset(set), .reset(reset));
endmodule
